// Logisim project calculator.circ as structural Verilog: 1 circuit, main circuit main
module main (
  input  ADD,
  input  SUBTRACT,
  input  MULTIPLY,
  input  DIVIDE,
  input  in_5,
  input  in_6,
  input  in_7,
  input  in_8,
  input  in_9,
  input  in_10,
  input  in_11,
  input  in_12,
  input  in_13,
  input  in_14,
  input  in_15,
  input  in_16
);

  wire main_1_out_13, main_1_out_14, main_1_out_15, main_1_out_16, main_1_out_17, main_1_out_18,
       main_2_out_7, main_2_out_8, main_2_out_9, main_2_out_10, main_2_out_11, main_2_out_12, main_2_out_13,
       main_2_out_14, main_2_out_15, main_2_out_16, main_2_out_17, main_2_out_18, main_2_out_19,
       main_2_out_20, main_2_out_21, main_2_out_22, main_3_out_14, main_3_out_15, main_3_out_16,
       main_3_out_17, main_3_out_18, main_3_out_19, main_4_out_14, main_4_out_15, main_4_out_16,
       main_4_out_17, main_4_out_18, main_4_out_19, main_5_out_7, main_5_out_8, main_5_out_9, main_5_out_10,
       main_5_out_11, main_5_out_12, main_5_out_13, main_5_out_14, main_5_out_15, main_5_out_16,
       main_5_out_17, main_5_out_18, main_5_out_19, main_5_out_20, main_5_out_21, main_5_out_22,
       main_6_out_14, main_6_out_15, main_6_out_16, main_6_out_17, main_6_out_18, main_6_out_19,
       main_7_out_14, main_7_out_15, main_7_out_16, main_7_out_17, main_7_out_18, main_7_out_19,
       main_8_out_7, main_8_out_8, main_8_out_9, main_8_out_10, main_8_out_11, main_8_out_12, main_8_out_13,
       main_8_out_14, main_8_out_15, main_8_out_16, main_8_out_17, main_8_out_18, main_8_out_19,
       main_8_out_20, main_8_out_21, main_8_out_22, main_9_p1, main_9_p2, main_9_p3, main_9_p4, main_9_p5,
       main_9_p6, main_10_p1, main_10_p2, main_10_p3, main_10_p4, main_10_p5, main_10_p6, main_11_out_14,
       main_11_out_15, main_11_out_16, main_11_out_17, main_11_out_18, main_11_out_19;

  subtraction_main main_1 (
    .in_7(in_11), .in_8(in_12), .in_9(in_13), .in_10(in_14), .in_11(in_15), .in_12(in_16),
    .out_15(main_1_out_15), .out_16(main_1_out_16), .out_17(main_1_out_17), .out_18(main_1_out_18),
    .in_1(in_5), .in_2(in_6), .in_3(in_7), .in_4(in_8), .in_5(in_9), .in_6(in_10), .out_13(main_1_out_13),
    .out_14(main_1_out_14));
  _7_Segment_Display u_7_segment_display_1 (
    .g(main_2_out_11), .f(main_2_out_12), .a(main_2_out_13), .b(main_2_out_14), .e(main_2_out_10),
    .d(main_2_out_9), .c(main_2_out_8), .dp(main_2_out_7));
  _7_Segment_Display u_7_segment_display_2 (
    .g(main_2_out_19), .f(main_2_out_20), .a(main_2_out_21), .b(main_2_out_22), .e(main_2_out_18),
    .d(main_2_out_17), .c(main_2_out_16), .dp(main_2_out_15));
  display_driver_main main_2 (
    .out_7(main_2_out_7), .out_8(main_2_out_8), .out_9(main_2_out_9), .out_10(main_2_out_10),
    .out_11(main_2_out_11), .out_12(main_2_out_12), .out_13(main_2_out_13), .out_14(main_2_out_14),
    .in_1(in_5), .in_2(in_6), .in_3(in_7), .in_4(in_8), .in_5(in_9), .in_6(in_10), .out_15(main_2_out_15),
    .out_16(main_2_out_16), .out_17(main_2_out_17), .out_18(main_2_out_18), .out_19(main_2_out_19),
    .out_20(main_2_out_20), .out_21(main_2_out_21), .out_22(main_2_out_22));
  addition_main main_3 (
    .in_1(in_5), .in_2(in_6), .in_3(in_7), .in_4(in_8), .in_5(in_9), .in_6(in_10), .in_7(in_11),
    .in_8(in_12), .in_9(in_13), .in_10(in_14), .in_11(in_15), .in_12(in_16), .out_14(main_3_out_14),
    .out_15(main_3_out_15), .out_16(main_3_out_16), .out_17(main_3_out_17), .out_18(main_3_out_18),
    .out_19(main_3_out_19));  // open: out_13
  output_selector_main main_4 (
    .in_7(SUBTRACT), .in_1(1'b0), .out_14(main_4_out_14), .in_2(1'b0), .out_15(main_4_out_15), .in_3(1'b0),
    .out_16(main_4_out_16), .in_4(1'b0), .out_17(main_4_out_17), .in_5(1'b0), .out_18(main_4_out_18),
    .in_6(1'b0), .out_19(main_4_out_19), .in_8(main_1_out_15), .in_9(main_1_out_16), .in_10(main_1_out_17),
    .in_11(main_1_out_18), .in_12(main_1_out_13), .in_13(main_1_out_14));
  _7_Segment_Display u_7_segment_display_3 (
    .g(main_5_out_11), .f(main_5_out_12), .a(main_5_out_13), .b(main_5_out_14), .e(main_5_out_10),
    .d(main_5_out_9), .c(main_5_out_8), .dp(main_5_out_7));
  display_driver_main main_5 (
    .out_7(main_5_out_7), .out_8(main_5_out_8), .out_9(main_5_out_9), .out_10(main_5_out_10),
    .out_11(main_5_out_11), .out_12(main_5_out_12), .out_13(main_5_out_13), .out_14(main_5_out_14),
    .in_1(in_11), .in_2(in_12), .in_3(in_13), .in_4(in_14), .in_5(in_15), .in_6(in_16),
    .out_15(main_5_out_15), .out_16(main_5_out_16), .out_17(main_5_out_17), .out_18(main_5_out_18),
    .out_19(main_5_out_19), .out_20(main_5_out_20), .out_21(main_5_out_21), .out_22(main_5_out_22));
  _7_Segment_Display u_7_segment_display_4 (
    .g(main_5_out_19), .f(main_5_out_20), .a(main_5_out_21), .b(main_5_out_22), .e(main_5_out_18),
    .d(main_5_out_17), .c(main_5_out_16), .dp(main_5_out_15));
  output_selector_main main_6 (
    .in_7(ADD), .in_1(main_11_out_14), .out_14(main_6_out_14), .in_2(main_11_out_15), .out_15(main_6_out_15),
    .in_3(main_11_out_16), .out_16(main_6_out_16), .in_4(main_11_out_17), .out_17(main_6_out_17),
    .in_5(main_11_out_18), .out_18(main_6_out_18), .in_6(main_11_out_19), .out_19(main_6_out_19),
    .in_8(main_3_out_14), .in_9(main_3_out_15), .in_10(main_3_out_16), .in_11(main_3_out_17),
    .in_12(main_3_out_18), .in_13(main_3_out_19));
  output_selector_main main_7 (
    .in_7(DIVIDE), .in_1(main_4_out_14), .out_14(main_7_out_14), .in_2(main_4_out_15),
    .out_15(main_7_out_15), .in_3(main_4_out_16), .out_16(main_7_out_16), .in_4(main_4_out_17),
    .out_17(main_7_out_17), .in_5(main_4_out_18), .out_18(main_7_out_18), .in_6(main_4_out_19),
    .out_19(main_7_out_19), .in_8(main_10_p1), .in_9(main_10_p2), .in_10(main_10_p3), .in_11(main_10_p4),
    .in_12(main_10_p5), .in_13(main_10_p6));
  _7_Segment_Display u_7_segment_display_5 (
    .g(main_8_out_19), .f(main_8_out_20), .a(main_8_out_21), .b(main_8_out_22), .e(main_8_out_18),
    .d(main_8_out_17), .c(main_8_out_16), .dp(main_8_out_15));
  _7_Segment_Display u_7_segment_display_6 (
    .g(main_8_out_11), .f(main_8_out_12), .a(main_8_out_13), .b(main_8_out_14), .e(main_8_out_10),
    .d(main_8_out_9), .c(main_8_out_8), .dp(main_8_out_7));
  display_driver_main main_8 (
    .out_7(main_8_out_7), .out_8(main_8_out_8), .out_9(main_8_out_9), .out_10(main_8_out_10),
    .out_11(main_8_out_11), .out_12(main_8_out_12), .out_13(main_8_out_13), .out_14(main_8_out_14),
    .in_1(main_6_out_14), .in_2(main_6_out_15), .in_3(main_6_out_16), .in_4(main_6_out_17),
    .in_5(main_6_out_18), .in_6(main_6_out_19), .out_15(main_8_out_15), .out_16(main_8_out_16),
    .out_17(main_8_out_17), .out_18(main_8_out_18), .out_19(main_8_out_19), .out_20(main_8_out_20),
    .out_21(main_8_out_21), .out_22(main_8_out_22));
  // multiplication_main main_9: pin names not known; wires that end beside it: main_9_p1, main_9_p2, main_9_p3, main_9_p4, main_9_p5, main_9_p6
  // division_main main_10: pin names not known; wires that end beside it: main_10_p1, main_10_p2, main_10_p3, main_10_p4, main_10_p5, main_10_p6, in_5, in_11
  output_selector_main main_11 (
    .in_7(MULTIPLY), .in_1(main_7_out_14), .out_14(main_11_out_14), .in_2(main_7_out_15),
    .out_15(main_11_out_15), .in_3(main_7_out_16), .out_16(main_11_out_16), .in_4(main_7_out_17),
    .out_17(main_11_out_17), .in_5(main_7_out_18), .out_18(main_11_out_18), .in_6(main_7_out_19),
    .out_19(main_11_out_19), .in_8(main_9_p1), .in_9(main_9_p2), .in_10(main_9_p3), .in_11(main_9_p4),
    .in_12(main_9_p5), .in_13(main_9_p6));
endmodule
