// Logisim project rudimentary computing device.circ as structural Verilog: 1 circuit, main circuit main
module main (
  input  in_1,
  input  [5:0] A,
  input  [5:0] B,
  input  [5:0] C,
  output [5:0] out_5,
  output [5:0] A_2,
  output [5:0] B_2,
  output [5:0] C_2
);

  wire and_1_out, and_2_out, and_3_out, and_4_out, and_5_out, and_6_out, and_7_out, and_8_out, and_9_out,
       button_1_out, button_2_out, clock_1_out, main_3_a_b, main_3_a_b_2, main_3_a_b_3, main_3_add,
       main_3_halt, main_3_insert, main_3_invert, main_3_out, main_3_step, not_1_out, or_1_out;
  wire [0:0] main_2_out_13, main_5_equality_check, main_6_out_13;
  wire [5:0] and_15_out, main_4_out_4, main_7_out_12, main_9_out_19, main_10_to_a, main_10_to_b,
       main_10_to_c, main_11_out_23, main_12_out_23, main_13_out_8, main_13_out_9, main_13_out_10,
       main_14_out_8, main_14_out_9, main_14_out_10, main_15_out_8, main_15_out_9, main_15_out_10,
       main_16_out_8, main_16_out_9, main_16_out_10, main_17_out_8, main_17_out_9, main_17_out_10,
       main_18_out_8, main_18_out_9, main_18_out_10, main_19_out_8, main_19_out_9, main_19_out_10,
       main_20_out_23;
  wire [31:0] rom_1_data;

  LED led_1 (.in(rom_1_data[31]));
  Button button_1 (.out(button_1_out));
  Clock clock_1 (.out(clock_1_out));
  Button button_2 (.out(button_2_out));
  not not_1 (not_1_out, button_1_out);
  and and_1 (and_1_out, rom_1_data[31], and_2_out);
  and and_2 (and_2_out, not_1_out, in_1);
  or or_1 (or_1_out, and_1_out, clock_1_out);
  and and_3 (and_3_out, in_1, main_3_halt);
  program_counter_main main_1 (
    .in_7(button_2_out), .in_8(or_1_out), .out_9(out_5[5]), .out_10(out_5[4]), .out_11(out_5[3]),
    .out_12(out_5[2]), .out_13(out_5[1]), .out_14(out_5[0]), .in_1(and_4_out), .in_2(and_5_out),
    .in_3(and_6_out), .in_4(and_7_out), .in_5(and_8_out), .in_6(and_9_out));
  and and_4 (and_4_out, in_1, and_15_out[5]);
  and and_5 (and_5_out, in_1, and_15_out[4]);
  and and_6 (and_6_out, in_1, and_15_out[3]);
  a_greater_than_b_main main_2 (
    .in_1(main_11_out_23[5]), .in_2(main_11_out_23[4]), .in_3(main_11_out_23[3]), .in_4(main_11_out_23[2]),
    .in_5(main_11_out_23[1]), .in_6(main_11_out_23[0]), .in_7(main_12_out_23[5]), .in_8(main_12_out_23[4]),
    .in_9(main_12_out_23[3]), .in_10(main_12_out_23[2]), .in_11(main_12_out_23[1]),
    .in_12(main_12_out_23[0]), .out_13(main_2_out_13[0]));
  instructor_main main_3 (
    .in_1(rom_1_data[30]), .in_2(rom_1_data[29]), .in_3(rom_1_data[28]), .in_4(rom_1_data[27]),
    .ADD(main_3_add), .INVERT(main_3_invert), .A_B(main_3_a_b), .A_B_2(main_3_a_b_2), .A_B_3(main_3_a_b_3),
    .STEP(main_3_step), .INSERT(main_3_insert), .OUT(main_3_out), .HALT(main_3_halt));  // open: out_14, out_15, out_16
  and and_7 (and_7_out, in_1, and_15_out[2]);
  step_selector_main main_4 (
    .in_2(main_20_out_23[0]), .in_1(main_11_out_23), .in_3(main_12_out_23), .out_4(main_4_out_4));
  equality_check_main main_5 (
    .Equality_Check(main_5_equality_check[0]), .in_1(main_11_out_23[5]), .in_2(main_11_out_23[4]),
    .Number_A(main_11_out_23[3]), .in_4(main_11_out_23[2]), .in_5(main_11_out_23[1]),
    .in_6(main_11_out_23[0]), .in_7(main_12_out_23[5]), .in_8(main_12_out_23[4]), .in_9(main_12_out_23[3]),
    .in_10(main_12_out_23[2]), .in_11(main_12_out_23[1]), .in_12(main_12_out_23[0]));
  a_less_than_b_main main_6 (
    .in_7(main_12_out_23[5]), .in_8(main_12_out_23[4]), .in_9(main_12_out_23[3]), .in_10(main_12_out_23[2]),
    .in_11(main_12_out_23[1]), .in_12(main_12_out_23[0]), .in_1(main_11_out_23[5]), .in_2(main_11_out_23[4]),
    .in_3(main_11_out_23[3]), .in_4(main_11_out_23[2]), .in_5(main_11_out_23[1]), .in_6(main_11_out_23[0]),
    .out_13(main_6_out_13[0]));
  inverter_main main_7 (
    .in_1(main_11_out_23[5]), .in_2(main_11_out_23[4]), .in_3(main_11_out_23[3]), .in_4(main_11_out_23[2]),
    .in_5(main_11_out_23[1]), .in_6(main_11_out_23[0]), .out_7(main_7_out_12[5]), .out_8(main_7_out_12[4]),
    .out_9(main_7_out_12[3]), .out_10(main_7_out_12[2]), .out_11(main_7_out_12[1]), .out_12(main_7_out_12[0]));
  input_selector_main main_8 (
    .in_4(main_3_out), .in_1({6{1'b0}}), .in_2({6{1'b0}}), .in_3({6{1'b0}}), .in_5(main_11_out_23),
    .in_6(main_12_out_23), .in_7(main_20_out_23), .out_8(A_2), .out_9(B_2), .out_10(C_2));
  and and_8 (and_8_out, in_1, and_15_out[1]);
  addition_main main_9 (
    .in_1(main_12_out_23[5]), .in_2(main_12_out_23[4]), .in_3(main_12_out_23[3]), .in_4(main_12_out_23[2]),
    .in_5(main_12_out_23[1]), .in_6(main_12_out_23[0]), .in_7(main_11_out_23[5]), .in_8(main_11_out_23[4]),
    .in_9(main_11_out_23[3]), .in_10(main_11_out_23[2]), .in_11(main_11_out_23[1]),
    .in_12(main_11_out_23[0]), .out_14(main_9_out_19[5]), .out_15(main_9_out_19[4]),
    .out_16(main_9_out_19[3]), .out_17(main_9_out_19[2]), .out_18(main_9_out_19[1]), .out_19(main_9_out_19[0]));  // open: out_13
  ROM #(.addrWidth(6), .dataWidth(32)) rom_1 (.addr(out_5), .data(rom_1_data));  // open: sel
  and and_9 (and_9_out, in_1, and_15_out[0]);
  value_transfer_main main_10 (
    .Inp_A(main_11_out_23), .Inp_C(main_20_out_23), .Inp_B(main_12_out_23), .To_B(main_10_to_b),
    .To_A(main_10_to_a), .To_C(main_10_to_c));
  and and_10 (and_15_out[5], main_4_out_4[5], main_3_step);
  memory_small_clocked_main main_11 (
    .Address(rom_1_data[23]), .in_6(rom_1_data[22]), .Write(rom_1_data[21]), .in_8(rom_1_data[20]),
    .Read(rom_1_data[19]), .Initialise(button_2_out), .in_12(main_19_out_8[5]), .in_13(main_19_out_8[4]),
    .Input(main_19_out_8[3]), .in_15(main_19_out_8[2]), .in_16(main_19_out_8[1]), .in_17(main_19_out_8[0]),
    .out_18(main_11_out_23[5]), .out_19(main_11_out_23[4]), .Output(main_11_out_23[3]),
    .out_21(main_11_out_23[2]), .out_22(main_11_out_23[1]), .out_23(main_11_out_23[0]),
    .in_4(rom_1_data[24]), .Alt(rom_1_data[25]), .in_2(rom_1_data[26]), .Pass(rom_1_data[18]), .Clk(or_1_out));
  and and_11 (and_15_out[4], main_4_out_4[4], main_3_step);
  and and_12 (and_15_out[3], main_4_out_4[3], main_3_step);
  and and_13 (and_15_out[2], main_4_out_4[2], main_3_step);
  memory_small_clocked_main main_12 (
    .Address(rom_1_data[14]), .in_6(rom_1_data[13]), .Write(rom_1_data[12]), .in_8(rom_1_data[11]),
    .Read(rom_1_data[10]), .Initialise(button_2_out), .in_12(main_19_out_9[5]), .in_13(main_19_out_9[4]),
    .Input(main_19_out_9[3]), .in_15(main_19_out_9[2]), .in_16(main_19_out_9[1]), .in_17(main_19_out_9[0]),
    .out_18(main_12_out_23[5]), .out_19(main_12_out_23[4]), .Output(main_12_out_23[3]),
    .out_21(main_12_out_23[2]), .out_22(main_12_out_23[1]), .out_23(main_12_out_23[0]),
    .in_4(rom_1_data[15]), .Alt(rom_1_data[16]), .in_2(rom_1_data[17]), .Pass(rom_1_data[9]), .Clk(or_1_out));
  and and_14 (and_15_out[1], main_4_out_4[1], main_3_step);
  and and_15 (and_15_out[0], main_4_out_4[0], main_3_step);
  input_selector_main main_13 (
    .in_4(and_3_out), .in_1({6{1'b0}}), .in_2({6{1'b0}}), .in_3({6{1'b0}}), .in_5(main_10_to_a),
    .in_6(main_10_to_b), .in_7(main_10_to_c), .out_8(main_13_out_8), .out_9(main_13_out_9),
    .out_10(main_13_out_10));
  input_selector_main main_14 (
    .in_4(main_3_a_b_3), .in_1(main_13_out_8), .in_2(main_13_out_9), .in_3(main_13_out_10), .in_5({6{1'b0}}),
    .in_6({6{1'b0}}), .in_7({{5{1'b0}}, main_5_equality_check[0]}), .out_8(main_14_out_8),
    .out_9(main_14_out_9), .out_10(main_14_out_10));
  input_selector_main main_15 (
    .in_4(main_3_a_b_2), .in_1(main_14_out_8), .in_2(main_14_out_9), .in_3(main_14_out_10), .in_5({6{1'b0}}),
    .in_6({6{1'b0}}), .in_7({{5{1'b0}}, main_6_out_13[0]}), .out_8(main_15_out_8), .out_9(main_15_out_9),
    .out_10(main_15_out_10));
  input_selector_main main_16 (
    .in_4(main_3_a_b), .in_1(main_15_out_8), .in_2(main_15_out_9), .in_3(main_15_out_10), .in_5({6{1'b0}}),
    .in_6({6{1'b0}}), .in_7({{5{1'b0}}, main_2_out_13[0]}), .out_8(main_16_out_8), .out_9(main_16_out_9),
    .out_10(main_16_out_10));
  input_selector_main main_17 (
    .in_4(main_3_invert), .in_1(main_16_out_8), .in_2(main_16_out_9), .in_3(main_16_out_10),
    .in_5({6{1'b0}}), .in_6({6{1'b0}}), .in_7(main_7_out_12), .out_8(main_17_out_8), .out_9(main_17_out_9),
    .out_10(main_17_out_10));
  input_selector_main main_18 (
    .in_4(main_3_insert), .in_1(main_17_out_8), .in_2(main_17_out_9), .in_3(main_17_out_10), .in_5(A),
    .in_6(B), .in_7(C), .out_8(main_18_out_8), .out_9(main_18_out_9), .out_10(main_18_out_10));
  input_selector_main main_19 (
    .in_4(main_3_add), .in_1(main_18_out_8), .in_2(main_18_out_9), .in_3(main_18_out_10), .in_5({6{1'b0}}),
    .in_6({6{1'b0}}), .in_7(main_9_out_19), .out_8(main_19_out_8), .out_9(main_19_out_9),
    .out_10(main_19_out_10));
  memory_small_clocked_main main_20 (
    .Address(rom_1_data[5]), .in_6(rom_1_data[4]), .Write(rom_1_data[3]), .in_8(rom_1_data[2]),
    .Read(rom_1_data[1]), .Initialise(button_2_out), .in_12(main_19_out_10[5]), .in_13(main_19_out_10[4]),
    .Input(main_19_out_10[3]), .in_15(main_19_out_10[2]), .in_16(main_19_out_10[1]),
    .in_17(main_19_out_10[0]), .out_18(main_20_out_23[5]), .out_19(main_20_out_23[4]),
    .Output(main_20_out_23[3]), .out_21(main_20_out_23[2]), .out_22(main_20_out_23[1]),
    .out_23(main_20_out_23[0]), .in_4(rom_1_data[6]), .Alt(rom_1_data[7]), .in_2(rom_1_data[8]),
    .Pass(rom_1_data[0]), .Clk(or_1_out));

  // Notes on the sheet:
  //   Counter
  //   Go
  //   Clock
  //   Initialise
  //   Set value to 1 after initialization
  //   Output
  //   Input
  //   contents of rom_1 (hex, n*v repeats v):
  //   0 4832f200 10e40014 48500012 0 48481214 48001812 4850020c 828140c 8481214 48500012 4830000a 2028721c
  //   3104e21a 48700012 48281800 c0681400
endmodule
